# Fritzing sketch real_wiring (saved by Fritzing 1.0.6)
breadboards: 1

parts:
  Mod1 = Raspberry Pi 4B
  R1 = Resistor [tolerance=±5% power=0.25W resistance=220 package=THT]
  R2 = Resistor [tolerance=±5% power=0.25W resistance=220 package=THT]
  R3 = Resistor [tolerance=±5% power=0.25W resistance=10k package=THT]
  S1 = Pushbutton [package=THT]
  R4 = Resistor [tolerance=±5% power=0.25W resistance=10k package=THT]
  R5 = Resistor [tolerance=±5% power=0.25W resistance=10k package=THT]
  R6 = Resistor [tolerance=±5% power=0.25W resistance=10k package=THT]
  S2 = Pushbutton [package=THT]
  S3 = Pushbutton [package=THT]
  S4 = Pushbutton [package=THT]
  LED1 = LED - 3mm [color="Red (633nm)" current=0.030A package="3 mm [THT]"]
  LED2 = LED - 3mm [color="Red (633nm)" current=0.030A package="3 mm [THT]"]
  Board1 = EPLZON PCB Prototype Board [package="Through-hole protoboard"]
  GPIO_Terminal_HAT1 = GeeekPi GPIO Screw Terminal Hat,Raspberry Pi GPIO Extension Board [package=Module]
  2_Relay_Module_5V1 = AZDelivery 2 Relay Module 5V Optocoupler [package=Module]
  R7 = Resistor [tolerance=±5% power=0.25W resistance=4.7k package=THT]
  R8 = Resistor [tolerance=±5% power=0.25W resistance=4.7k package=THT]
  R9 = Resistor [tolerance=±5% power=0.25W resistance=4.7k package=THT]
  R10 = Resistor [tolerance=±5% power=0.25W resistance=4.7k package=THT]
  S5 = Pushbutton [package=THT]
  S6 = Pushbutton [package=THT]
  S7 = Pushbutton [package=THT]
  S8 = Pushbutton [package=THT]
  C5 = Electrolytic Capacitor [capacitance=0.47mF voltage=16V package="100 mil [THT, electrolytic]"]
  C12 = Tantalum Capacitor [capacitance=100nF voltage=35V package="100 mil [THT, tantalum]"]  # not connected
  C13 = Tantalum Capacitor [capacitance=100nF voltage=35V package="100 mil [THT, tantalum]"]
  C14 = Electrolytic Capacitor [capacitance=100µF voltage=35V package="100 mil [THT, electrolytic]"]
  C15 = Tantalum Capacitor [capacitance=100nF voltage=35V package="100 mil [THT, tantalum]"]
  C16 = Tantalum Capacitor [capacitance=100nF voltage=35V package="100 mil [THT, tantalum]"]
  C17 = Tantalum Capacitor [capacitance=100nF voltage=35V package="100 mil [THT, tantalum]"]
  C18 = Tantalum Capacitor [capacitance=100nF voltage=35V package="100 mil [THT, tantalum]"]
  Bornier_2_pins1 = Bornier 2 pins
  Bornier_2_pins2 = Bornier 2 pins
  Bornier_2_pins3 = Bornier 2 pins  # not connected
  Bornier_2_pins4 = Bornier 2 pins  # not connected

nets:
  N1: Mod1.3V3, R3.Pin_1, R4.Pin_1, R5.Pin_1, R6.Pin_1
  N2: Mod1.GND, R1.Pin_0, R2.Pin_0, S1.leg1, S2.leg1, S3.leg1, S4.leg1
  N3: Mod1.GPIO17, R3.Pin_0, S1.leg0
  N4: Mod1.GPIO27, R4.Pin_0, S2.leg0
  N5: Mod1.GPIO22, R5.Pin_0, S3.leg0
  N6: Mod1.GPIO23, R6.Pin_0, S4.leg0
  N7: Mod1.GPIO24, LED1.anode
  N8: Mod1.GPIO25, LED2.anode
  N9: R1.Pin_1, LED1.cathode
  N10: R2.Pin_1, LED2.cathode
  N11: Board1.R01C03, Board1.R01C05, Board1.R01C09, Board1.R01C10, Board1.R01C15, Board1.R01C21, Board1.R01C24, Board1.R01C25, Board1.R01C26, Board1.R01C27, Board1.R01C28, Board1.R01C30, Board1.R03C05, Board1.R03C09, Board1.R03C15, Board1.R03C21, Board1.R05C05, Board1.R05C09, Board1.R05C15, Board1.R05C21, Board1.R07C09, Board1.R13C01, Board1.R13C03, Board1.R13C09, Board1.R13C19, GPIO_Terminal_HAT1.GND_1, GPIO_Terminal_HAT1.GND_7, GPIO_Terminal_HAT1.GND_8, 2_Relay_Module_5V1.GND, S5.leg0, S6.leg0, S7.leg0, S8.leg0, C5.-, C13.-, C14.-, C15.-, C16.-, C17.-, C18.-
  N12: Board1.R02C01, Board1.R02C02, Board1.R02C07, Board1.R02C10, Board1.R02C11, Board1.R02C17, Board1.R02C23, Board1.R02C28, Board1.R02C30, GPIO_Terminal_HAT1.3V3_1, R7.Pin_0, R8.Pin_0, R9.Pin_0, R10.Pin_0, C13.+, C14.+
  N13: Board1.R03C07, Board1.R04C07, Board1.R05C07, Board1.R07C07, Board1.R08C07, Board1.R10C07, Board1.R12C07, GPIO_Terminal_HAT1.IO23, R7.Pin_1, S5.leg1, C15.+, Bornier_2_pins1.1, Bornier_2_pins1.2
  N14: Board1.R03C11, Board1.R04C11, Board1.R05C11, Board1.R07C11, Board1.R08C11, Board1.R10C11, Board1.R12C11, GPIO_Terminal_HAT1.IO22, R8.Pin_1, S6.leg1, C16.+, Bornier_2_pins2.1, Bornier_2_pins2.2
  N15: Board1.R03C17, Board1.R04C17, Board1.R05C17, Board1.R07C17, Board1.R08C17, Board1.R10C17, Board1.R12C17, GPIO_Terminal_HAT1.IO20, R10.Pin_1, S7.leg1, C17.+
  N16: Board1.R03C23, Board1.R04C23, Board1.R05C23, Board1.R07C23, Board1.R08C23, Board1.R12C23, R9.Pin_1, C18.+
  N17: Board1.R11C24, Board1.R12C24, GPIO_Terminal_HAT1.IO19, S8.leg1
  N18: Board1.R14C01, Board1.R14C02, Board1.R14C19, Board1.R14C30, GPIO_Terminal_HAT1.5V_1, GPIO_Terminal_HAT1.5V_2, 2_Relay_Module_5V1.VCC, C5.+
  N19: GPIO_Terminal_HAT1.IO24, 2_Relay_Module_5V1.IN2
  N20: GPIO_Terminal_HAT1.IO25, 2_Relay_Module_5V1.IN1

notes:
  Fonction
  GPIO BCM
  Pin physique
  Flotteur 1 (bas)
  GPIO17
  Pin 11
  Flotteur 2
  GPIO27
  Pin 13
  Flotteur 3
  GPIO22
  Pin 15
  Flotteur 4 (haut)
  GPIO23
  Pin 16
  Relais pompe
  GPIO24
  Pin 18
  Relais vanne
  GPIO25
  Pin 22
  GND
  -
  Pins 6, 9, 14
  3.3V
  -
  Pin 1
  5V
  -
  Pin 2

custom parts:
  EPLZON PCB Prototype Board: Passive 88.9mm x 52.1mm prototype board reconstructed from a top-view photo. Each visible plated through-hole is exposed as an independent connector. The four corner mounting holes are decorative only.
  GeeekPi GPIO Screw Terminal Hat,Raspberry Pi GPIO Extension Board: 40-position Raspberry Pi GPIO screw terminal breakout HAT reconstructed from the provided top and bare-board images. Breadboard connectors are aligned to the four rows of ten screw terminals for practical wire attachment in Fritzing.
  AZDelivery 2 Relay Module 5V Optocoupler: 2-channel 5V relay module with optocouplers, based on the provided AZDelivery top-view photo.
  Bornier 2 pins: Bornier a vis 2 positions, entraxe 5 mm, composant generique neutre.
