# Fritzing sketch test_pi_breadboard_optimized (saved by Fritzing 1.0.6)
breadboards: 1

parts:
  Mod1 = Raspberry Pi 4B
  R1 = Resistor [tolerance=±5% power=0.25W resistance=220 package=THT]
  R2 = Resistor [tolerance=±5% power=0.25W resistance=220 package=THT]
  R3 = Resistor [tolerance=±5% power=0.25W resistance=10k package=THT]
  S1 = Pushbutton [package=THT]
  R4 = Resistor [tolerance=±5% power=0.25W resistance=10k package=THT]
  R5 = Resistor [tolerance=±5% power=0.25W resistance=10k package=THT]
  R6 = Resistor [tolerance=±5% power=0.25W resistance=10k package=THT]
  S3 = Pushbutton [package=THT]
  S4 = Pushbutton [package=THT]
  LED1 = LED - 3mm [color="Red (633nm)" current=0.030A package="3 mm [THT]"]
  LED2 = LED - 3mm [color="Red (633nm)" current=0.030A package="3 mm [THT]"]
  S5 = Pushbutton [package=THT]

nets:
  N1: Mod1.3V3, R3.Pin_1, R4.Pin_1, R5.Pin_1, R6.Pin_1
  N2: Mod1.GND, R1.Pin_0, R2.Pin_0, S1.leg1, S3.leg1, S4.leg1, S5.leg1
  N3: Mod1.GPIO17, R3.Pin_0, S1.leg0
  N4: Mod1.GPIO27, R4.Pin_0, S5.leg0
  N5: Mod1.GPIO22, R5.Pin_0, S3.leg0
  N6: Mod1.GPIO23, R6.Pin_0, S4.leg0
  N7: Mod1.GPIO24, LED1.anode
  N8: Mod1.GPIO25, LED2.anode
  N9: R1.Pin_1, LED1.cathode
  N10: R2.Pin_1, LED2.cathode

notes:
  Fonction
  GPIO BCM
  Pin physique
  Flotteur 1 (bas)
  GPIO17
  Pin 11
  Flotteur 2
  GPIO27
  Pin 13
  Flotteur 3
  GPIO22
  Pin 15
  Flotteur 4 (haut)
  GPIO23
  Pin 16
  Relais pompe
  GPIO24
  Pin 18
  Relais vanne
  GPIO25
  Pin 22
  GND
  -
  Pins 6, 9, 14
  3.3V
  -
  Pin 1
  5V
  -
  Pin 2
